// Logisim project Master.circ as structural Verilog: 5 circuits, main circuit main
module main (
  output [3:0] Destination,
  output [7:0] DMem_Adress,
  output Destination_Enabler,
  output [3:0] Source,
  output Source_Enabler,
  output [7:0] SMem_Adress,
  output Clock
);

  wire Add, and_2_out, and_4_out, and_11_out, clock_1_out, Group_0, Group_1, Group_2, Group_3, Group_4, HALT,
       Mul, not_2_out, not_3_out, not_4_out, not_5_out, not_6_out, not_7_out, not_8_out, not_9_out,
       not_10_out, not_11_out, not_12_out, not_13_out, not_14_out, not_15_out, not_16_out, or_3_out,
       or_4_out, RRMov, Subtract_On;
  wire [3:0] Group, Instruction;
  wire [4:0] pc_1_out_3;
  wire [7:0] R0, R1, R2, R3, R4, R5, R6, R7, RegA, RegB;

  Clock clock_1 (.out(clock_1_out));
  not not_1 (Clock, clock_1_out);
  PC pc_1 (.out_3(pc_1_out_3), .HALT(HALT), .Clk(Clock));
  not not_2 (not_2_out, Group[3]);
  not not_3 (not_3_out, Group[2]);
  not not_4 (not_4_out, Group[0]);
  not not_5 (not_5_out, Group[1]);
  and and_1 (Group_0, not_4_out, not_5_out, not_3_out, not_2_out);
  LED led_1 (.in(Group_0));
  and and_2 (and_2_out, Group_3, Instruction[0], Instruction[1], ~Instruction[2], ~Instruction[3]);  // AND_Gate
  LED led_2 (.in(and_2_out));
  not not_6 (not_6_out, Group[3]);
  not not_7 (not_7_out, Group[2]);
  not not_8 (not_8_out, Group[0]);
  not not_9 (not_9_out, Group[1]);
  and and_3 (Group_1, Group[0], not_9_out, not_7_out, not_6_out);
  LED led_3 (.in(Group_1));
  and and_4 (and_4_out, Group_3, ~Instruction[0], Instruction[1], Instruction[2], ~Instruction[3]);  // AND_Gate
  LED led_4 (.in(and_4_out));
  ROM #(.addrWidth(5), .dataWidth(24)) rom_1 (
    .addr(pc_1_out_3), .data({Group, Instruction, SMem_Adress, DMem_Adress[7:4], Destination}));  // open: sel
  not not_10 (not_10_out, Group[2]);
  not not_11 (not_11_out, Group[3]);
  and and_5 (Group_3, Group[0], Group[1], not_14_out, not_12_out);
  and and_6 (Group_2, not_8_out, Group[1], not_10_out, not_11_out);
  LED led_5 (.in(Group_3));
  LED led_6 (.in(Group_2));
  not not_12 (not_12_out, Group[3]);
  not not_13 (not_13_out, Group[1]);
  not not_14 (not_14_out, Group[2]);
  not not_15 (not_15_out, Group[0]);
  not not_16 (not_16_out, Group[3]);
  and and_7 (Group_4, not_15_out, not_13_out, Group[2], not_16_out);
  LED led_7 (.in(Group_4));
  and and_8 (Add, Group_2, Instruction[0], Instruction[1], Instruction[2], ~Instruction[3]);  // AND_Gate
  LED led_8 (.in(Add));
  and and_9 (Mul, Group_2, Instruction[0], ~Instruction[1], ~Instruction[2], Instruction[3]);  // AND_Gate
  LED led_9 (.in(Mul));
  and and_10 (RRMov, Group_2, ~Instruction[0], Instruction[1], ~Instruction[2], ~Instruction[3]);  // AND_Gate
  and and_11 (and_11_out, Group_2, ~Instruction[0], ~Instruction[1], ~Instruction[2]);  // AND_Gate
  LED led_10 (.in(RRMov));
  LED led_11 (.in(and_11_out));
  Decoder #(.select(4)) decoder_1 (
    .out0(HALT), .out8(Subtract_On), .sel(Instruction));  // open: out1, out2, out3, out4, out5, out6, out7, out9, out10, out11, out12, out13, out14, out15, en
  or or_1 (Destination_Enabler, Group_2, Group_1, Group_3);
  or or_2 (Source_Enabler, Group_2, Group_4, Group_3);
  or or_3 (or_3_out, Group_2, Group_4, Group_3);
  or or_4 (or_4_out, Group_2, Group_1, Group_3);
  Multiplexer #(.select(4), .width(8)) multiplexer_1 (
    .in1(R0), .in2(R1), .in3(R2), .in4(R3), .in5(R4), .in6(R5), .in7(R6), .in8(R7), .out(RegA),
    .sel(SMem_Adress[3:0]), .en(or_3_out));  // open: in0, in9, in10, in11, in12, in13, in14, in15
  Multiplexer #(.select(4), .width(8)) multiplexer_2 (
    .in1(R0), .in2(R1), .in3(R2), .in4(R3), .in5(R4), .in6(R5), .in7(R6), .in8(R7), .out(RegB),
    .sel(Destination), .en(or_4_out));  // open: in0, in9, in10, in11, in12, in13, in14, in15

  assign DMem_Adress[3:0] = Destination;
  assign Source = SMem_Adress[3:0];

  // Other names for the same wires on the sheet: Dest_Mem_Adress[7:0] = {DMem_Adress[7:4], Destination};
  //   Source_Mem_Adress[7:0] = SMem_Adress

  // Notes on the sheet:
  //   halt
  //   ldm
  //   IRMov
  //   stm
  //   contents of rom_1 (hex, n*v repeats v):
  //   270102 290805 115c07 220604 4bff00 0 4a1b00 280301 330203 5407ab 360408 5505bf
  //   Instructions
  //   help
endmodule

module Register_Bank (
  input  [7:0] ALU_Input,
  output [3:0] out_2,
  output [7:0] R0,
  output [7:0] R1,
  output [7:0] R2,
  output [7:0] R3,
  output [7:0] R4,
  output [7:0] R5,
  output [7:0] R6,
  output [7:0] R7
);

  wire and_1_out, Clock, decoder_1_out1, decoder_1_out2, decoder_1_out3, decoder_1_out4, decoder_1_out5,
       decoder_1_out6, decoder_1_out7, decoder_1_out8, Dest_Enabler;

  main main_1 (
    .Destination(out_2), .Destination_Enabler(Dest_Enabler), .Clock(Clock));  // open: DMem_Adress, Source, Source_Enabler, SMem_Adress
  Decoder #(.select(4)) decoder_1 (
    .out1(decoder_1_out1), .out2(decoder_1_out2), .out3(decoder_1_out3), .out4(decoder_1_out4),
    .out5(decoder_1_out5), .out6(decoder_1_out6), .out7(decoder_1_out7), .out8(decoder_1_out8), .sel(out_2),
    .en(Dest_Enabler));  // open: out0, out9, out10, out11, out12, out13, out14, out15
  and and_1 (and_1_out, Clock, Dest_Enabler);
  Register u_R0 (.Clock(and_1_out), .Enable(decoder_1_out1), .Input(ALU_Input), .out_4(R0));
  Register u_R1 (.Clock(and_1_out), .Enable(decoder_1_out2), .Input(ALU_Input), .out_4(R1));
  Register u_R2 (.Clock(and_1_out), .Enable(decoder_1_out3), .Input(ALU_Input), .out_4(R2));
  Register u_R3 (.Clock(and_1_out), .Enable(decoder_1_out4), .Input(ALU_Input), .out_4(R3));
  Register u_R4 (.Clock(and_1_out), .Enable(decoder_1_out5), .Input(ALU_Input), .out_4(R4));
  Register u_R5 (.Clock(and_1_out), .Enable(decoder_1_out6), .Input(ALU_Input), .out_4(R5));
  Register u_R6 (.Clock(and_1_out), .Enable(decoder_1_out7), .Input(ALU_Input), .out_4(R6));
  Register u_R7 (.Clock(and_1_out), .Enable(decoder_1_out8), .Input(ALU_Input), .out_4(R7));

  // Other names for the same wires on the sheet: Dest[3:0] = out_2
endmodule

module Register (
  input  Clock,
  input  Enable,
  input  [7:0] Input,
  output [7:0] out_4
);

  D_Flip_Flop d_ff_1 (.clk(Clock), .D(Input[0]), .Q(out_4[0]), .en(Enable));  // open: Qn, preset, reset
  D_Flip_Flop d_ff_2 (.clk(Clock), .D(Input[1]), .Q(out_4[1]), .en(Enable));  // open: Qn, preset, reset
  D_Flip_Flop d_ff_3 (.clk(Clock), .D(Input[2]), .Q(out_4[2]), .en(Enable));  // open: Qn, preset, reset
  D_Flip_Flop d_ff_4 (.clk(Clock), .D(Input[3]), .Q(out_4[3]), .en(Enable));  // open: Qn, preset, reset
  D_Flip_Flop d_ff_5 (.clk(Clock), .D(Input[4]), .Q(out_4[4]), .en(Enable));  // open: Qn, preset, reset
  D_Flip_Flop d_ff_6 (.clk(Clock), .D(Input[5]), .Q(out_4[5]), .en(Enable));  // open: Qn, preset, reset
  D_Flip_Flop d_ff_7 (.clk(Clock), .D(Input[6]), .Q(out_4[6]), .en(Enable));  // open: Qn, preset, reset
  D_Flip_Flop d_ff_8 (.clk(Clock), .D(Input[7]), .Q(out_4[7]), .en(Enable));  // open: Qn, preset, reset
endmodule

module ALUI (
  output [7:0] out_1
);

  Register_Bank register_bank_1 (.R0(out_1));  // open: ALU_Input, out_2, R1, R2, R3, R4, R5, R6, R7
endmodule

module PC (
  input  HALT,
  input  Clk,
  output [4:0] out_3
);

  wire and_1_out, t_ff_1_qn, t_ff_2_qn, t_ff_3_qn, t_ff_4_qn;

  T_Flip_Flop t_ff_1 (.clk(and_1_out), .T(1'b1), .Q(out_3[0]), .Qn(t_ff_1_qn));  // open: preset, reset, en
  and and_1 (and_1_out, ~HALT, Clk);  // AND_Gate
  T_Flip_Flop t_ff_2 (.clk(t_ff_1_qn), .T(1'b1), .Q(out_3[1]), .Qn(t_ff_2_qn));  // open: preset, reset, en
  T_Flip_Flop t_ff_3 (.clk(t_ff_2_qn), .T(1'b1), .Q(out_3[2]), .Qn(t_ff_3_qn));  // open: preset, reset, en
  T_Flip_Flop t_ff_4 (.clk(t_ff_3_qn), .T(1'b1), .Q(out_3[3]), .Qn(t_ff_4_qn));  // open: preset, reset, en
  T_Flip_Flop t_ff_5 (.clk(t_ff_4_qn), .T(1'b1), .Q(out_3[4]));  // open: Qn, preset, reset, en
endmodule
